// Logisim project lab07_starter.circ as structural Verilog: 3 circuits, main circuit register_file
module register_file (
  input  [3:0] data_write,
  input  clear,
  input  write_enable,
  input  [1:0] read_reg,
  input  [1:0] write_reg,
  input  clk,
  output [3:0] data_read
);

  wire demultiplexer_1_out0, demultiplexer_1_out1, demultiplexer_1_out2, demultiplexer_1_out3;
  wire [3:0] multiplexer_1_out, reg0_q, reg1_q, reg2_q, reg3_q;

  Multiplexer #(.width(4), .enable("false")) multiplexer_1 (
    .in0(data_write), .in1(4'b0000), .out(multiplexer_1_out), .sel(clear));
  Demultiplexer #(.select(2), .enable("false")) demultiplexer_1 (
    .out0(demultiplexer_1_out0), .out1(demultiplexer_1_out1), .out2(demultiplexer_1_out2),
    .out3(demultiplexer_1_out3), .in(write_enable), .sel(write_reg));
  Register #(.width(4)) reg0 (.D(multiplexer_1_out), .en(demultiplexer_1_out0), .clk(clk), .Q(reg0_q));  // open: clr
  Register #(.width(4)) reg1 (.D(multiplexer_1_out), .en(demultiplexer_1_out1), .clk(clk), .Q(reg1_q));  // open: clr
  Register #(.width(4)) reg2 (.D(multiplexer_1_out), .en(demultiplexer_1_out2), .clk(clk), .Q(reg2_q));  // open: clr
  Register #(.width(4)) reg3 (.D(multiplexer_1_out), .en(demultiplexer_1_out3), .clk(clk), .Q(reg3_q));  // open: clr
  Multiplexer #(.select(2), .width(4), .enable("false")) multiplexer_2 (
    .in0(reg0_q), .in1(reg1_q), .in2(reg2_q), .in3(reg3_q), .out(data_read), .sel(read_reg));
endmodule

module alu (
  input  [3:0] A,
  input  [3:0] B,
  input  op,
  output [3:0] data_out
);
endmodule

module instr_decoder (
  input  [7:0] instr,
  output [1:0] imm,
  output [1:0] read_reg,
  output [1:0] write_reg,
  output write_en,
  output alu_op,
  output reg_clear
);
endmodule
