// Logisim project lab2.circ as structural Verilog: 8 circuits, main circuit main
module main (
  input  in_1,
  input  in_2,
  input  in_3
);

  wire seg0_1_out0, seg1_1_out1, seg2_1_out2, seg3_1_out3, seg4_1_out4, seg5_1_out5, seg6_1_out6;

  Seg1 seg1_1 (.A(in_1), .B(in_2), .C(in_3), .Out1(seg1_1_out1));
  Seg0 seg0_1 (.A(in_1), .B(in_2), .C(in_3), .Out0(seg0_1_out0));
  Seg5 seg5_1 (.A(in_1), .B(in_2), .C(in_3), .Out5(seg5_1_out5));
  Seg6 seg6_1 (.B(in_2), .C(in_3), .Out6(seg6_1_out6));
  Seg4 seg4_1 (.A(in_1), .C(in_3), .Out4(seg4_1_out4));
  Seg3 seg3_1 (.B(in_2), .Out3(seg3_1_out3));
  _7_Segment_Display u_7_segment_display_1 (
    .g(seg6_1_out6), .f(seg5_1_out5), .a(seg0_1_out0), .b(seg1_1_out1), .e(seg4_1_out4), .d(seg3_1_out3),
    .c(seg2_1_out2));  // open: dp
  Seg2 seg2_1 (.A(in_1), .B(in_2), .C(in_3), .Out2(seg2_1_out2));
endmodule

module Seg0 (
  input  A,
  input  B,
  input  C,
  output Out0
);

  wire and_1_out, and_2_out, not_1_out, not_2_out, not_3_out;

  not not_1 (not_1_out, A);
  not not_2 (not_2_out, B);
  not not_3 (not_3_out, C);
  and and_1 (and_1_out, A, not_2_out, not_3_out);
  and and_2 (and_2_out, not_1_out, not_2_out, C);
  or or_1 (Out0, and_2_out, and_1_out);
endmodule

module Seg1 (
  input  A,
  input  B,
  input  C,
  output Out1
);

  wire and_1_out, and_2_out, not_1_out, not_2_out;

  not not_1 (not_1_out, A);
  not not_2 (not_2_out, B);
  and and_1 (and_1_out, not_1_out, not_2_out);
  and and_2 (and_2_out, not_1_out, C);
  or or_1 (Out1, and_1_out, and_2_out);
endmodule

module Seg2 (
  input  A,
  input  B,
  input  C,
  output Out2
);

  wire and_1_out, not_1_out, not_2_out;

  not not_1 (not_1_out, A);
  not not_2 (not_2_out, B);
  and and_1 (and_1_out, not_1_out, not_2_out);
  or or_1 (Out2, and_1_out, C);
endmodule

module Seg3 (
  input  B,
  output Out3
);

  not not_1 (Out3, B);
endmodule

module Seg4 (
  input  A,
  input  C,
  output Out4
);

  or or_1 (Out4, A, C);
endmodule

module Seg5 (
  input  A,
  input  B,
  input  C,
  output Out5
);

  wire and_1_out, and_2_out, and_3_out, not_1_out, not_2_out, not_3_out;

  not not_1 (not_1_out, A);
  not not_2 (not_2_out, B);
  not not_3 (not_3_out, C);
  and and_1 (and_1_out, not_1_out, not_2_out);
  and and_2 (and_2_out, not_3_out, A);
  and and_3 (and_3_out, not_1_out, C);
  or or_1 (Out5, and_1_out, and_2_out, and_3_out);
endmodule

module Seg6 (
  input  B,
  input  C,
  output Out6
);

  wire and_1_out, and_2_out, not_1_out, not_2_out;

  not not_1 (not_1_out, B);
  not not_2 (not_2_out, C);
  and and_1 (and_1_out, B, C);
  and and_2 (and_2_out, not_1_out, not_2_out);
  or or_1 (Out6, and_1_out, and_2_out);
endmodule
