// Logisim project lab4.circ as structural Verilog: 4 circuits, main circuit SRLatch
module main (
  input  S,
  input  in_2,
  input  R,
  input  in_4,
  input  D,
  input  in_6,
  input  Din,
  output NotQ,
  output Q,
  output out_10,
  output out_11,
  output out_12
);

  SRLatch srlatch_1 (.S(S), .CLK(in_2), .R(R), .NotQ(NotQ), .Q(Q));
  DLatch dlatch_1 (.CLK(in_4), .D(D), .Q(out_10), .NotQ(out_11));
  Dflipflop dflipflop_1 (.CLK(in_6), .D(Din), .Q(out_12));
endmodule

module SRLatch (
  input  S,
  input  CLK,
  input  R,
  output NotQ,
  output Q
);

  wire and_1_out, and_2_out;

  and and_1 (and_1_out, S, CLK);
  and and_2 (and_2_out, CLK, R);
  nor nor_1 (NotQ, and_1_out, Q);
  nor nor_2 (Q, NotQ, and_2_out);
endmodule

module DLatch (
  input  CLK,
  input  D,
  output Q,
  output NotQ
);

  wire and_1_out, and_2_out, not_1_out;

  not not_1 (not_1_out, D);
  and and_1 (and_1_out, not_1_out, CLK);
  and and_2 (and_2_out, CLK, D);
  nor nor_1 (Q, and_1_out, NotQ);
  nor nor_2 (NotQ, Q, and_2_out);
endmodule

module Dflipflop (
  input  CLK,
  input  D,
  output Q
);

  wire dlatch_1_q, not_1_out;

  not not_1 (not_1_out, CLK);
  DLatch dlatch_1 (.CLK(not_1_out), .D(D), .Q(dlatch_1_q));  // open: NotQ
  DLatch dlatch_2 (.CLK(CLK), .D(dlatch_1_q), .Q(Q));  // open: NotQ

  // Notes on the sheet:
  //   Q1
  //   Q2
endmodule
