// Logisim project lab7.circ as structural Verilog: 4 circuits, main circuit register_file
module register_file (
  input  [3:0] data_write,
  input  clear,
  input  write_enable,
  input  [1:0] read_reg,
  input  [1:0] write_reg,
  input  clk,
  output [3:0] data_read
);

  wire demultiplexer_1_out0, demultiplexer_1_out1, demultiplexer_1_out2, demultiplexer_1_out3;
  wire [3:0] multiplexer_1_out, reg0_q, reg1_q, reg2_q, reg3_q;

  Multiplexer #(.enable("false"), .width(4)) multiplexer_1 (
    .in0(data_write), .in1(4'b0000), .out(multiplexer_1_out), .sel(clear));
  Demultiplexer #(.enable("false"), .select(2)) demultiplexer_1 (
    .out0(demultiplexer_1_out0), .out1(demultiplexer_1_out1), .out2(demultiplexer_1_out2),
    .out3(demultiplexer_1_out3), .in(write_enable), .sel(write_reg));
  Register #(.width(4)) reg0 (.D(multiplexer_1_out), .en(demultiplexer_1_out0), .clk(clk), .Q(reg0_q));  // open: clr
  Register #(.width(4)) reg1 (.D(multiplexer_1_out), .en(demultiplexer_1_out1), .clk(clk), .Q(reg1_q));  // open: clr
  Register #(.width(4)) reg2 (.D(multiplexer_1_out), .en(demultiplexer_1_out2), .clk(clk), .Q(reg2_q));  // open: clr
  Register #(.width(4)) reg3 (.D(multiplexer_1_out), .en(demultiplexer_1_out3), .clk(clk), .Q(reg3_q));  // open: clr
  Multiplexer #(.enable("false"), .select(2), .width(4)) multiplexer_2 (
    .in0(reg0_q), .in1(reg1_q), .in2(reg2_q), .in3(reg3_q), .out(data_read), .sel(read_reg));

  // Notes on the sheet:
  //   Bus -4 bits
  //   Bus -4 bits
  //   Bus -2 bits
  //   Bus -4 bits
  //   Bus -4 bits
  //   Bus -4 bits
  //   Bus -4 bits
  //   Bus -4 bits
  //   Bus -4 bits
  //   Bus -4 bits
  //   Bus -2 bits
  //   Bus -4 bits
endmodule

module alu (
  input  [3:0] A,
  input  [3:0] B,
  input  op,
  output [3:0] data_out
);

  wire [3:0] adder_1_out, subtractor_1_out;

  Adder #(.width(4)) adder_1 (.a(A), .b(B), .out(adder_1_out));  // open: cin, cout
  Subtractor #(.width(4)) subtractor_1 (.a(A), .b(B), .out(subtractor_1_out));  // open: bin, bout
  Multiplexer #(.enable("false"), .width(4)) multiplexer_1 (
    .in0(adder_1_out), .in1(subtractor_1_out), .out(data_out), .sel(op));

  // Notes on the sheet:
  //   Bus -4 bits
  //   Bus -4 bits
  //   Bus -4 bits
  //   Bus -4 bits
  //   Bus -4 bits
  //   Bus -4 bits
  //   Bus -4 bits
  //   Bus -4 bits
endmodule

module instr_decoder (
  input  [7:0] instr,
  output [1:0] imm,
  output [1:0] read_reg,
  output [1:0] write_reg,
  output write_en,
  output alu_op,
  output reg_clear
);

  and and_1 (reg_clear, instr[6], instr[7]);
  or or_1 (write_en, instr[6], instr[7]);

  assign alu_op = instr[6];
  assign imm = instr[1:0];
  assign read_reg = instr[3:2];
  assign write_reg = instr[5:4];

  // Notes on the sheet:
  //   Bus -8 bits
  //   Bus -2 bits
  //   Bus -2 bits
  //   Bus -2 bits
  //   Bus -2 bits
endmodule

module main (
  input  [7:0] INSTR,
  input  CLK
);

  wire instr_decoder_1_alu_op, instr_decoder_1_reg_clear, instr_decoder_1_write_en;
  wire [1:0] instr_decoder_1_imm, instr_decoder_1_read_reg, instr_decoder_1_write_reg;
  wire [3:0] alu_1_data_out, bit_extender_1_out, register_file_1_data_read;

  instr_decoder instr_decoder_1 (
    .instr(INSTR), .imm(instr_decoder_1_imm), .read_reg(instr_decoder_1_read_reg),
    .write_reg(instr_decoder_1_write_reg), .write_en(instr_decoder_1_write_en),
    .alu_op(instr_decoder_1_alu_op), .reg_clear(instr_decoder_1_reg_clear));
  assign bit_extender_1_out = {{2{1'b0}}, instr_decoder_1_imm};  // Bit_Extender bit_extender_1
  register_file register_file_1 (
    .data_write(alu_1_data_out), .clear(instr_decoder_1_reg_clear), .write_enable(instr_decoder_1_write_en),
    .read_reg(instr_decoder_1_read_reg), .write_reg(instr_decoder_1_write_reg), .clk(CLK),
    .data_read(register_file_1_data_read));
  alu alu_1 (
    .A(register_file_1_data_read), .B(bit_extender_1_out), .op(instr_decoder_1_alu_op),
    .data_out(alu_1_data_out));

  // Notes on the sheet:
  //   Bus -8 bits
  //   Bus -8 bits
  //   Bus -2 bits
  //   Bus -2 bits
  //   Bus -2 bits
  //   Bus -4 bits
  //   Bus -4 bits
  //   Bus -4 bits
endmodule
